# Fritzing sketch Untitled Sketch (saved by Fritzing 0.8.7b)

parts:
  Part1 = Arduino Ethernet Shield (Rev3)
  Part2 = Real Time Clock Module - DS1307 RTC Breakout Board
  RHT1 = Humidity and Temperature Sensor RHT03
  R1 = Resistor [tolerance=±5% resistance=10k package=THT]

nets:
  N1: Part1.A4/SDA, Part2.SDA
  N2: Part1.A5/SCL, Part2.SCL
  N3: Part1.D2, RHT1.Data-signal, R1.Pin_0
  5V: Part1.5V, Part2.5V, R1.Pin_1
  GND: Part1.GND, Part2.GND
